// Logisim project SPM.circ as structural Verilog: 1 circuit, main circuit main
module main (
  input  A_0,
  input  A_1,
  input  A_2,
  input  in_4,
  input  RST
);

  wire adder_1_cout, adder_1_out, adder_2_cout, adder_2_out, and_1_out, and_2_out, and_3_out, and_4_out,
       and_5_out, B_out, CLK_out, d_ff_1_q, d_ff_2_q, d_ff_3_q, d_ff_4_q, d_ff_5_q, d_ff_6_q, or_1_out,
       xor_1_out, xor_2_out, xor_3_out, xor_4_out, xor_5_out;

  Clock CLK (.out(CLK_out));
  Shift_Register #(.length(3)) B (
    .in(in_4), .clk(CLK_out), .out(B_out), .clr(RST));  // open: shift, load, d0, q0, d1, q1, d2, q2
  and and_1 (and_1_out, A_0, B_out);
  or or_1 (or_1_out, and_1_out, d_ff_1_q);
  xor xor_1 (xor_1_out, and_1_out, d_ff_1_q);
  D_Flip_Flop #(.trigger("high")) d_ff_1 (
    .clk(CLK_out), .D(or_1_out), .Q(d_ff_1_q), .reset(RST));  // open: Qn, preset, en
  D_Flip_Flop #(.trigger("high")) d_ff_2 (
    .clk(CLK_out), .D(xor_1_out), .Q(d_ff_2_q), .reset(RST));  // open: Qn, preset, en
  and and_2 (and_2_out, A_1, B_out);
  and and_3 (and_3_out, adder_1_out, and_2_out);
  Adder #(.width(1)) adder_1 (.a(d_ff_2_q), .b(d_ff_4_q), .out(adder_1_out), .cout(adder_1_cout));  // open: cin
  xor xor_2 (xor_2_out, and_2_out, adder_1_out);
  xor xor_3 (xor_3_out, and_3_out, adder_1_cout);
  D_Flip_Flop d_ff_3 (.clk(CLK_out), .D(xor_2_out), .Q(d_ff_3_q), .reset(RST));  // open: Qn, preset, en
  D_Flip_Flop d_ff_4 (.clk(CLK_out), .D(xor_3_out), .Q(d_ff_4_q), .reset(RST));  // open: Qn, preset, en
  and and_4 (and_4_out, A_2, B_out);
  and and_5 (and_5_out, adder_2_out, and_4_out);
  xor xor_4 (xor_4_out, and_4_out, adder_2_out);
  Adder #(.width(1)) adder_2 (.a(d_ff_3_q), .b(d_ff_5_q), .out(adder_2_out), .cout(adder_2_cout));  // open: cin
  xor xor_5 (xor_5_out, and_5_out, adder_2_cout);
  D_Flip_Flop d_ff_5 (.clk(CLK_out), .D(xor_5_out), .Q(d_ff_5_q), .reset(RST));  // open: Qn, preset, en
  D_Flip_Flop d_ff_6 (.clk(CLK_out), .D(xor_4_out), .Q(d_ff_6_q), .reset(RST));  // open: Qn, preset, en
  Shift_Register #(.length(6)) shift_register_1 (
    .in(d_ff_6_q), .clk(CLK_out), .clr(RST));  // open: shift, out, load, d0, q0, d1, q1, d2, q2, d3, q3, d4, q4, d5, q5
endmodule
